# Fritzing sketch v2 fritz  (saved by Fritzing 0.9.3b)
breadboards: 1

parts:
  Part1 = Arduino Uno (Rev3)
  R1 = Resistor [tolerance=±5% resistance=220 package=THT]
  LED1 = LED - 5mm [color="Red (633nm)" package="5 mm [THT]"]
  J1 = Piezo Speaker

nets:
  N1: Part1.GND, LED1.cathode, J1.pin1
  N2: Part1.D3_PWM, J1.pin2
  N3: Part1.D4, R1.Pin_0
  N4: R1.Pin_1, LED1.anode
